// Logisim project Basic_Components.circ as structural Verilog
module JKFlipFLop (
  input  J,
  input  CLK,
  input  K,
  output Q,
  output n_Q
);

  wire nand_1_out, nand_2_out;

  nand nand_1 (nand_1_out, n_Q, J, CLK);
  nand nand_2 (nand_2_out, CLK, K, Q);
  nand nand_3 (Q, nand_1_out, n_Q);
  nand nand_4 (n_Q, Q, nand_2_out);
endmodule

module Register_8b (
  input  CLK,
  input  [7:0] J,
  input  [7:0] K,
  output [7:0] Q,
  output [7:0] n_Q
);

  wire nand_1_out, nand_2_out, nand_3_out, nand_4_out, nand_5_out, nand_6_out, nand_7_out, nand_8_out,
       nand_9_out, nand_10_out, nand_11_out, nand_12_out, nand_13_out, nand_14_out, nand_15_out, nand_16_out,
       nand_17_out, nand_18_out, nand_19_out, nand_20_out, nand_21_out, nand_22_out, nand_23_out,
       nand_24_out, nand_25_out, nand_26_out, nand_27_out, nand_28_out, nand_29_out, nand_30_out,
       nand_31_out, nand_32_out, undriven, undriven_2, undriven_3, undriven_4, undriven_5, undriven_6,
       undriven_7, undriven_8, undriven_9, undriven_10, undriven_11, undriven_12, undriven_13, undriven_14,
       undriven_15, undriven_16;

  Multiplexer #(.select(3)) multiplexer_1 ();  // open: in0, in1, in2, in3, in4, in5, in6, in7, out, sel
  Demultiplexer #(.select(3)) demultiplexer_1 ();  // open: out0, out1, out2, out3, out4, out5, out6, out7, in, sel
  nand nand_1 (nand_1_out, nand_18_out, undriven, CLK);
  nand nand_2 (nand_2_out, CLK, undriven_2, nand_17_out);
  nand nand_3 (nand_3_out, nand_20_out, undriven_3, CLK);
  nand nand_4 (nand_4_out, CLK, undriven_4, nand_19_out);
  nand nand_5 (nand_5_out, nand_22_out, undriven_5, CLK);
  nand nand_6 (nand_6_out, CLK, undriven_6, nand_21_out);
  nand nand_7 (nand_7_out, nand_24_out, undriven_7, CLK);
  nand nand_8 (nand_8_out, CLK, undriven_8, nand_23_out);
  nand nand_9 (nand_9_out, nand_26_out, undriven_9, CLK);
  nand nand_10 (nand_10_out, CLK, undriven_10, nand_25_out);
  nand nand_11 (nand_11_out, nand_28_out, undriven_11, CLK);
  nand nand_12 (nand_12_out, CLK, undriven_12, nand_27_out);
  nand nand_13 (nand_13_out, nand_30_out, undriven_13, CLK);
  nand nand_14 (nand_14_out, CLK, undriven_14, nand_29_out);
  nand nand_15 (nand_15_out, nand_32_out, undriven_15, CLK);
  nand nand_16 (nand_16_out, CLK, undriven_16, nand_31_out);
  nand nand_17 (nand_17_out, nand_1_out, nand_18_out);
  nand nand_18 (nand_18_out, nand_17_out, nand_2_out);
  nand nand_19 (nand_19_out, nand_3_out, nand_20_out);
  nand nand_20 (nand_20_out, nand_19_out, nand_4_out);
  nand nand_21 (nand_21_out, nand_5_out, nand_22_out);
  nand nand_22 (nand_22_out, nand_21_out, nand_6_out);
  nand nand_23 (nand_23_out, nand_7_out, nand_24_out);
  nand nand_24 (nand_24_out, nand_23_out, nand_8_out);
  nand nand_25 (nand_25_out, nand_9_out, nand_26_out);
  nand nand_26 (nand_26_out, nand_25_out, nand_10_out);
  nand nand_27 (nand_27_out, nand_11_out, nand_28_out);
  nand nand_28 (nand_28_out, nand_27_out, nand_12_out);
  nand nand_29 (nand_29_out, nand_13_out, nand_30_out);
  nand nand_30 (nand_30_out, nand_29_out, nand_14_out);
  nand nand_31 (nand_31_out, nand_15_out, nand_32_out);
  nand nand_32 (nand_32_out, nand_31_out, nand_16_out);
endmodule

module MUX (
  input  [2:0] S,
  input  [7:0] D,
  output O
);

  wire and_1_out, and_2_out, and_3_out, and_4_out, and_5_out, and_6_out, and_7_out, and_8_out, not_1_out,
       not_2_out, not_3_out;

  not not_1 (not_1_out, S[2]);
  not not_2 (not_2_out, S[1]);
  not not_3 (not_3_out, S[0]);
  and and_1 (and_1_out, not_3_out, not_2_out, not_1_out, D[0]);
  and and_2 (and_2_out, S[0], not_2_out, not_1_out, D[1]);
  and and_3 (and_3_out, not_3_out, S[1], not_1_out, D[2]);
  and and_4 (and_4_out, S[0], S[1], not_1_out, D[3]);
  and and_5 (and_5_out, not_3_out, not_2_out, S[2], D[4]);
  and and_6 (and_6_out, S[0], not_2_out, S[2], D[5]);
  and and_7 (and_7_out, not_3_out, S[1], S[2], D[6]);
  and and_8 (and_8_out, S[0], S[1], S[2], D[7]);
  or or_1 (O, and_1_out, and_2_out, and_3_out, and_4_out, and_5_out, and_6_out, and_7_out, and_8_out);
endmodule

module DMX (
  input  [2:0] S,
  input  D,
  output [7:0] O
);

  wire not_1_out, not_2_out, not_3_out;

  not not_1 (not_1_out, S[2]);
  not not_2 (not_2_out, S[1]);
  not not_3 (not_3_out, S[0]);
  and and_1 (O[0], not_3_out, not_2_out, not_1_out, D);
  and and_2 (O[1], S[0], not_2_out, not_1_out, D);
  and and_3 (O[2], not_3_out, S[1], not_1_out, D);
  and and_4 (O[3], S[0], S[1], not_1_out, D);
  and and_5 (O[4], not_3_out, not_2_out, S[2], D);
  and and_6 (O[5], S[0], not_2_out, S[2], D);
  and and_7 (O[6], not_3_out, S[1], S[2], D);
  and and_8 (O[7], S[0], S[1], S[2], D);
endmodule
