// Logisim project SAP_2.circ as structural Verilog: 4 circuits, main circuit main
module main (
);

  wire [7:0] pc_1_out_2, pc_1_out_2_2;

  PC pc_1 (.in_1({pc_1_out_2_2, pc_1_out_2}), .out_2({pc_1_out_2_2, pc_1_out_2}));
  MAR mar_1 (.in_1({pc_1_out_2_2, pc_1_out_2}));  // open: out_2
  MDR mdr_1 (.out_3(pc_1_out_2), .out_4(pc_1_out_2));  // open: in_1, in_2
  Hex_Digit_Display hex_digit_display_1 ();  // open: value, dp
  Hex_Digit_Display hex_digit_display_2 ();  // open: value, dp
  Hex_Digit_Display #(.decimalPoint("false")) hex_digit_display_3 (.value(pc_1_out_2_2[7:4]));
  Hex_Digit_Display #(.decimalPoint("false")) hex_digit_display_4 (.value(pc_1_out_2_2[3:0]));
  Hex_Digit_Display #(.decimalPoint("false")) hex_digit_display_5 (.value(pc_1_out_2[7:4]));
  Hex_Digit_Display #(.decimalPoint("false")) hex_digit_display_6 (.value(pc_1_out_2[3:0]));
endmodule

module PC (
  input  [15:0] in_1,
  output [15:0] out_2
);

  wire undriven, undriven_2, undriven_3, undriven_4;
  wire [15:0] j_k_ff_16_q;

  J_K_Flip_Flop #(.trigger("falling")) j_k_ff_1 (
    .J(undriven_2), .K(undriven_2), .clk(undriven_3), .Q(j_k_ff_16_q[15]), .reset(undriven_4));  // open: Qn, preset
  J_K_Flip_Flop #(.trigger("falling")) j_k_ff_2 (
    .J(undriven_2), .K(undriven_2), .clk(j_k_ff_16_q[15]), .Q(j_k_ff_16_q[14]), .reset(undriven_4));  // open: Qn, preset
  J_K_Flip_Flop #(.trigger("falling")) j_k_ff_3 (
    .J(undriven_2), .K(undriven_2), .clk(j_k_ff_16_q[14]), .Q(j_k_ff_16_q[13]), .reset(undriven_4));  // open: Qn, preset
  J_K_Flip_Flop #(.trigger("falling")) j_k_ff_4 (
    .J(undriven_2), .K(undriven_2), .clk(j_k_ff_16_q[13]), .Q(j_k_ff_16_q[12]), .reset(undriven_4));  // open: Qn, preset
  J_K_Flip_Flop #(.trigger("falling")) j_k_ff_5 (
    .J(undriven_2), .K(undriven_2), .clk(j_k_ff_16_q[12]), .Q(j_k_ff_16_q[11]), .reset(undriven_4));  // open: Qn, preset
  J_K_Flip_Flop #(.trigger("falling")) j_k_ff_6 (
    .J(undriven_2), .K(undriven_2), .clk(j_k_ff_16_q[11]), .Q(j_k_ff_16_q[10]), .reset(undriven_4));  // open: Qn, preset
  J_K_Flip_Flop #(.trigger("falling")) j_k_ff_7 (
    .J(undriven_2), .K(undriven_2), .clk(j_k_ff_16_q[10]), .Q(j_k_ff_16_q[9]), .reset(undriven_4));  // open: Qn, preset
  J_K_Flip_Flop #(.trigger("falling")) j_k_ff_8 (
    .J(undriven_2), .K(undriven_2), .clk(j_k_ff_16_q[9]), .Q(j_k_ff_16_q[8]), .reset(undriven_4));  // open: Qn, preset
  J_K_Flip_Flop #(.trigger("falling")) j_k_ff_9 (
    .J(undriven_2), .K(undriven_2), .clk(j_k_ff_16_q[8]), .Q(j_k_ff_16_q[7]), .reset(undriven_4));  // open: Qn, preset
  J_K_Flip_Flop #(.trigger("falling")) j_k_ff_10 (
    .J(undriven_2), .K(undriven_2), .clk(j_k_ff_16_q[7]), .Q(j_k_ff_16_q[6]), .reset(undriven_4));  // open: Qn, preset
  assign out_2 = undriven ? j_k_ff_16_q : 16'bz;  // Controlled_Buffer controlled_buffer_1
  J_K_Flip_Flop #(.trigger("falling")) j_k_ff_11 (
    .J(undriven_2), .K(undriven_2), .clk(j_k_ff_16_q[6]), .Q(j_k_ff_16_q[5]), .reset(undriven_4));  // open: Qn, preset
  J_K_Flip_Flop #(.trigger("falling")) j_k_ff_12 (
    .J(undriven_2), .K(undriven_2), .clk(j_k_ff_16_q[5]), .Q(j_k_ff_16_q[4]), .reset(undriven_4));  // open: Qn, preset
  J_K_Flip_Flop #(.trigger("falling")) j_k_ff_13 (
    .J(undriven_2), .K(undriven_2), .clk(j_k_ff_16_q[4]), .Q(j_k_ff_16_q[3]), .reset(undriven_4));  // open: Qn, preset
  J_K_Flip_Flop #(.trigger("falling")) j_k_ff_14 (
    .J(undriven_2), .K(undriven_2), .clk(j_k_ff_16_q[3]), .Q(j_k_ff_16_q[2]), .reset(undriven_4));  // open: Qn, preset
  J_K_Flip_Flop #(.trigger("falling")) j_k_ff_15 (
    .J(undriven_2), .K(undriven_2), .clk(j_k_ff_16_q[2]), .Q(j_k_ff_16_q[1]), .reset(undriven_4));  // open: Qn, preset
  J_K_Flip_Flop #(.trigger("falling")) j_k_ff_16 (
    .J(undriven_2), .K(undriven_2), .clk(j_k_ff_16_q[1]), .Q(j_k_ff_16_q[0]), .reset(undriven_4));  // open: Qn, preset
endmodule

module MAR (
  input  [15:0] in_1,
  output [15:0] out_2
);


  assign out_2 = in_1;
endmodule

module MDR (
  input  [7:0] in_1,
  input  [7:0] in_2,
  output [7:0] out_3,
  output [7:0] out_4
);


  assign out_3 = in_2;
  assign out_4 = in_1;
endmodule
